# Fritzing sketch leduino (saved by Fritzing 0.9.1b)
breadboards: 1

parts:
  Part1 = Arduino Uno (Rev3)
  R4 = Resistor [tolerance=±5% resistance=330 package="0805 [SMD]"]
  LED2 = smd LED [color="Red (633nm)" package="0603 [SMD]"]

nets:
  N1: Part1.D13/SCK, R4.Pin_0
  N2: Part1.GND, LED2.cathode
  N3: R4.Pin_1, LED2.anode
